# Fritzing sketch duco_esp-01 (saved by Fritzing 0.9.6b)

parts:
  ESP-01 = ESP8266 ESP01 [part_number=ESP8266 package=THT]
  DUCO_Box_Silent_UART = JST XH 5A [part_number=U1]
  C1 = Capacitor Polarized [part_number=C1 package=cpol-radial-10uf-25v]

nets:
  N1: ESP-01.GND, DUCO_Box_Silent_UART.pin4, C1.-
  N2: ESP-01.RXD, DUCO_Box_Silent_UART.pin1
  N3: ESP-01.TXD, DUCO_Box_Silent_UART.pin2
  N4: ESP-01.VCC, ESP-01.CH_PD, DUCO_Box_Silent_UART.pin5, C1.+

notes:
  GND
  Vcc 3.3v
  U0RXD
  U0TXD
  Ch_EN

custom parts:
  ESP8266 ESP01: Generic WiFi Module based on the ESP8266 with onboard PCB antenna and UART communications
  JST XH 5A: JST XH 5A 2.54.mm
